# Fritzing sketch blinds (saved by Fritzing 0.9.10b)
breadboards: 1

parts:
  R1 = Resistor [tolerance=±5% power=0.25 resistance=10k package=THT]
  Part1 = Arduino Uno (Rev3)
  R2 = Photocell (LDR) [package=THT]
  J1 = Basic Servo

nets:
  N1: R1.Pin_0, Part1.A1, R2.pin_1
  GND: R1.Pin_1, Part1.GND, J1.gnd
  N2: Part1.D9_PWM, J1.pulse
  5V: Part1.5V, R2.pin_0, J1.vcc
